# Fritzing sketch Proyecto Cascodrilo (saved by Fritzing 0.9.3b)
breadboards: 1

parts:
  Componente1 = Arduino Uno (Rev3)
  J1 = Basic Servo
  Componente2 = Bluetooth HC-05 Macho
  M1 = DC Motor
  M2 = DC Motor
  S1 = H-Bridge with L298N
  VCC1 = Battery
  VCC2 = Battery
  J2 = Basic Servo

nets:
  N1: Componente1.D8, S1.IN1
  N2: Componente1.D9_PWM, S1.IN2
  N3: Componente1.D12/MISO, S1.IN4
  N4: Componente1.D13/SCK, S1.IN3
  N5: Componente1.D2, Componente2.TXD
  N6: Componente1.D3_PWM, Componente2.RXD
  5V: Componente1.5V, Componente2.VCC
  GND: Componente1.GND, J1.gnd, Componente2.GND, S1.GND, VCC1.-, VCC2.-, J2.gnd
  VIN: Componente1.VIN, S1.5V
  VCC: J1.vcc, VCC2.+, J2.vcc
  N7: M1.pin_1, S1.M2-02
  N8: M1.pin_2, S1.M2-01
  N9: M2.pin_1, S1.M1-01
  N10: M2.pin_2, S1.M1-02
  N11: S1.12V, VCC1.+

custom parts:
  H-Bridge with L298N: h-bridge
